# Fritzing sketch pcb_demo_fritzing (saved by Fritzing 0.9.10b)
breadboards: 1

parts:
  BAT1 = Battery Holders [package=battcom_20mm_pth]
  IC1 = IC, DIP package, 14 pins [chip_label=IC]
  R1 = Photocell (LDR) [package=THT]
  C1 = Ceramic Capacitor [capacitance=100nF voltage=35V package="100 mil [THT, multilayer]"]
  SG1 = Buzzer 12mm [part_number=COM-07950 package=buzzer-12mm-ns]
  S1 = Pushbutton [package=THT]
  R2 = Resistor [tolerance=±5% power=0.25 resistance=1k package=THT]
  C2 = Electrolytic Capacitor [capacitance=1µF voltage=35V package="100 mil [THT, electrolytic]"]
  LED1 = LED - 5mm [color="Yellow (585nm)" current=0.030 package="5 mm [THT]"]
  R3 = Resistor [tolerance=±5% power=0.25 resistance=1k package=THT]

nets:
  N1: BAT1.+, S1.leg1
  N2: BAT1.-, IC1.pin7, C1.1, SG1.2, C2.-, LED1.cathode
  N3: IC1.pin1, R1.pin_1, C1.0
  N4: IC1.pin2, IC1.pin3, R1.pin_0
  N5: IC1.pin4, SG1.1
  N6: IC1.pin14, S1.leg0, R2.Pin_1, R3.Pin_1
  N7: R2.Pin_0, C2.+
  N8: LED1.anode, R3.Pin_0

notes:
  40106

custom parts:
  Buzzer 12mm: Buzzer 12mm Spark Fun Electronics SKU : Comp-Buzzer Through hole This is a small 12mm round speaker that operates around the audible 2kHz range. You can use these speakers to create simple music or user interfaces. This is not a true piezoelectric speaker but behaves similarly. Instead of a piezoelectric crystal that vibrates with an electric current, this tiny speaker uses an electromagnet to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
